// Logisim project TallerLogica-Combinatorios.circ as structural Verilog: 11 circuits, main circuit verificador
module sumador_simple (
  input  a,
  input  b,
  output S,
  output Cout
);

  xor xor_1 (S, a, b);
  and and_1 (Cout, a, b);
endmodule

module sumador_completo (
  input  Cin,
  input  A,
  input  B,
  output S,
  output Cout
);

  wire and_1_out, and_2_out, xor_1_out;

  xor xor_1 (xor_1_out, A, B);
  and and_1 (and_1_out, A, B);
  xor xor_2 (S, Cin, xor_1_out);
  and and_2 (and_2_out, Cin, xor_1_out);
  or or_1 (Cout, and_1_out, and_2_out);
endmodule

// sum 4bits
module sumador4 (
  input  Cin,
  input  [3:0] A,
  input  [3:0] B,
  output [3:0] S,
  output Cout
);

  wire Ful_Adder_2_cout, Ful_Adder_3_cout, Ful_Adder_cout;

  sumador_completo Ful_Adder (.A(A[0]), .B(B[0]), .Cin(Cin), .S(S[0]), .Cout(Ful_Adder_cout));
  sumador_completo Ful_Adder_2 (.A(A[1]), .B(B[1]), .Cin(Ful_Adder_cout), .S(S[1]), .Cout(Ful_Adder_2_cout));
  sumador_completo Ful_Adder_3 (.A(A[2]), .B(B[2]), .Cin(Ful_Adder_2_cout), .S(S[2]), .Cout(Ful_Adder_3_cout));
  sumador_completo Ful_Adder_4 (.A(B[3]), .B(A[3]), .Cin(Ful_Adder_3_cout), .S(S[3]), .Cout(Cout));
  Hex_Digit_Display hex_digit_display_1 (.value(S));  // open: dp
endmodule

module comparador_cero (
  input  [3:0] A,
  output Z
);

  wire or_1_out, or_2_out, or_3_out;

  or or_1 (or_1_out, A[0], A[1]);
  or or_2 (or_2_out, A[2], A[3]);
  or or_3 (or_3_out, or_1_out, or_2_out);
  not not_1 (Z, or_3_out);
endmodule

module sumador_flags (
  input  Cin,
  input  [3:0] A,
  input  [3:0] B,
  output [3:0] S,
  output V,
  output C,
  output Z,
  output N
);

  wire and_1_out, and_2_out, not_1_out, not_2_out, not_3_out;

  and and_1 (and_1_out, B[3], A[3], not_3_out);
  not not_1 (not_1_out, B[3]);
  not not_2 (not_2_out, A[3]);
  and and_2 (and_2_out, not_2_out, not_1_out, N);
  or or_1 (V, and_1_out, and_2_out);
  sumador4 sumador4_1 (.Cin(Cin), .A(A), .S({N, S[2:0]}), .B(B), .Cout(C));
  Hex_Digit_Display hex_digit_display_1 (.value({N, S[2:0]}));  // open: dp
  comparador_cero comparador_cero_1 (.A({N, S[2:0]}), .Z(Z));
  not not_3 (not_3_out, N);

  assign S[3] = N;
endmodule

module incrementador_4 (
  input  [3:0] A,
  output [3:0] S
);

  wire sumador_simple_1_cout, sumador_simple_2_cout, sumador_simple_3_cout;

  sumador_simple sumador_simple_1 (.a(1'b1), .b(A[0]), .S(S[0]), .Cout(sumador_simple_1_cout));
  sumador_simple sumador_simple_2 (.a(A[1]), .b(sumador_simple_1_cout), .S(S[1]), .Cout(sumador_simple_2_cout));
  sumador_simple sumador_simple_3 (.a(sumador_simple_2_cout), .b(A[2]), .S(S[2]), .Cout(sumador_simple_3_cout));
  sumador_simple sumador_simple_4 (.a(sumador_simple_3_cout), .b(A[3]), .S(S[3]));  // open: Cout
  Hex_Digit_Display hex_digit_display_1 (.value(S));  // open: dp
endmodule

module inversor_4 (
  input  [3:0] A,
  input  INV,
  output [3:0] S
);

  wire [3:0] incrementador_4_1_s, not_1_out;

  not not_1 (not_1_out[0], A[0]);
  not not_2 (not_1_out[1], A[1]);
  not not_3 (not_1_out[2], A[2]);
  not not_4 (not_1_out[3], A[3]);
  incrementador_4 incrementador_4_1 (.A(not_1_out), .S(incrementador_4_1_s));
  Hex_Digit_Display hex_digit_display_1 (.value(S));  // open: dp
  Multiplexer #(.width(4)) multiplexer_1 (.in0(A), .in1(incrementador_4_1_s), .out(S), .sel(INV));  // open: en
endmodule

module ALU (
  input  [3:0] A,
  input  [3:0] B,
  input  [1:0] OP,
  output N,
  output Z,
  output V,
  output C,
  output [3:0] S
);

  wire compAcero_2_z, compAcero_z, not_1_out, sumador_4_flags_2_c, sumador_4_flags_2_n, sumador_4_flags_2_v,
       sumador_4_flags_2_z, sumador_4_flags_c, sumador_4_flags_n, sumador_4_flags_v, sumador_4_flags_z;
  wire [3:0] AND_4_s, inv4_s, OR_4_s, sumador_4_flags_2_s, sumador_4_flags_s;

  sumador_flags sumador_4_flags (
    .A(A), .B(B), .Cin(1'b0), .V(sumador_4_flags_v), .C(sumador_4_flags_c), .Z(sumador_4_flags_z),
    .N(sumador_4_flags_n), .S(sumador_4_flags_s));
  inversor_4 inv4 (.A(B), .INV(1'b1), .S(inv4_s));
  sumador_flags sumador_4_flags_2 (
    .A(inv4_s), .B(A), .Cin(1'b0), .V(sumador_4_flags_2_v), .C(sumador_4_flags_2_c), .Z(sumador_4_flags_2_z),
    .N(sumador_4_flags_2_n), .S(sumador_4_flags_2_s));
  not not_1 (not_1_out, sumador_4_flags_2_c);
  OR_4 OR_4 (.A(A), .B(B), .S(OR_4_s));
  AND_4 AND_4 (.A(B), .B(A), .S(AND_4_s));
  Multiplexer #(.select(2)) multiplexer_1 (
    .in0(sumador_4_flags_c), .in1(not_1_out), .in2(1'b0), .in3(1'b0), .out(C), .sel(OP));  // open: en
  Multiplexer #(.select(2)) multiplexer_2 (
    .in0(sumador_4_flags_v), .in1(sumador_4_flags_2_v), .in2(1'b0), .in3(1'b0), .out(V), .sel(OP));  // open: en
  comparador_cero compAcero (.A(AND_4_s), .Z(compAcero_z));
  comparador_cero compAcero_2 (.A(OR_4_s), .Z(compAcero_2_z));
  Multiplexer #(.select(2)) multiplexer_3 (
    .in0(sumador_4_flags_z), .in1(sumador_4_flags_2_z), .in2(compAcero_2_z), .in3(compAcero_z), .out(Z),
    .sel(OP));  // open: en
  Multiplexer #(.select(2)) multiplexer_4 (
    .in0(sumador_4_flags_n), .in1(sumador_4_flags_2_n), .in2(AND_4_s[3]), .in3(OR_4_s[3]), .out(N), .sel(OP));  // open: en
  Hex_Digit_Display hex_digit_display_1 (.value(S));  // open: dp
  Multiplexer #(.select(2), .width(4)) multiplexer_5 (
    .in0(sumador_4_flags_s), .in1(sumador_4_flags_2_s), .in2(AND_4_s), .in3(OR_4_s), .out(S), .sel(OP));  // open: en
endmodule

module verificador (
  output [3:0] a,
  output [3:0] b,
  output [1:0] Op,
  output N,
  output Z,
  output V,
  output C,
  output [3:0] Res,
  output halt
);

  wire clock_1_out;

  Clock clock_1 (.out(clock_1_out));
  Counter #(.width(10), .max('h3ff)) counter_1 (
    .Q({Op, b, a}), .carry(halt), .clk(clock_1_out));  // open: load, D, count, clr
  // ALU alu_1: pin names not known; wires that end beside it: a, b, Op, N, Z, V, C, Res
endmodule

module OR_4 (
  input  [3:0] A,
  input  [3:0] B,
  output [3:0] S
);

  or or_1 (S[0], A[0], B[0]);
  or or_2 (S[1], A[1], B[1]);
  or or_3 (S[2], A[2], B[2]);
  or or_4 (S[3], A[3], B[3]);
endmodule

module AND_4 (
  input  [3:0] A,
  input  [3:0] B,
  output [3:0] S
);

  and and_1 (S[0], A[0], B[0]);
  and and_2 (S[1], A[1], B[1]);
  and and_3 (S[2], A[2], B[2]);
  and and_4 (S[3], A[3], B[3]);
endmodule
